# Fritzing sketch Untitled Sketch (saved by Fritzing 1.0.1rc)

parts:
  A1 = WeMos D1 R1
  LED1 = smd LED [color="Red (633nm)" package="1206 [SMD]"]
  LED2 = smd LED [color="Green (570nm)" package="1206 [SMD]"]
  S1 = Pushbutton [package="[SMD]"]
  DS1 = DS18B20 1-Wire Temperature Sensor [part_number=DS18B20]
  DS3 = DS18B20 1-Wire Temperature Sensor [part_number=DS18B20]
  R1 = RPACK* [package=rpack-sip-pth-5]
  R2 = RPACK* [package=rpack-sip-pth-5]
  R4 = Resistor [tolerance=±5% resistance=220 package="0402 [SMD]"]
  R5 = Resistor [tolerance=±5% resistance=220 package="0402 [SMD]"]
  R6 = Resistor [tolerance=±5% power=0.25 resistance=220 package=THT]

nets:
  N1: A1.Pin_9, A1.Pin_10, R2.1, R2.2, R5.Pin_1
  N2: A1.Pin_12, A1.Pin_66, R1.1
  N3: A1.Pin_41, S1.Pin_1, S1.Pin_2, R6.Pin_1
  N4: A1.Pin_49, DS3.DQ, R5.Pin_0
  N5: A1.Pin_51, A1.Pin_63, LED1.anode
  N6: A1.Pin_53, A1.Pin_61, LED2.anode
  N7: LED1.cathode, R1.2
  N8: LED2.cathode, R1.4
  N9: S1.Pin_4, R1.3
  N10: DS1.GND, R1.6
  N11: DS1.DQ, R4.Pin_0
  N12: DS1.VDD, R2.4, R4.Pin_1
  N13: DS3.GND, R1.5
  N14: DS3.VDD, R2.3

custom parts:
  WeMos D1 R1: The WeMos D1 is a ESP8266 WiFi based board that uses the Arduino layout with a operating voltage of 3.3V.
