# Fritzing sketch 2sensoresWifi05 (saved by Fritzing 1.0.1rc)

parts:
  A1 = WeMos D1 R1
  DS2 = DS18B20 1-Wire Temperature Sensor Probe
  DS1 = DS18B20 1-Wire Temperature Sensor Probe
  LED1 = smd LED [color="Red (633nm)" package="0805 [SMD]"]
  LED2 = smd LED [color="Green (565nm)" package="0805 [SMD]"]
  JP1_Positivo_5v = Header 12 [package=1x12_machine-pin-header_lock.004]
  JP2_Neutro_(GRN) = Header 12 [package=1x12_machine-pin-header_lock.004]
  S1 = Pushbutton [package="[THT]"]
  R3 = Resistor [package="2010 [SMD]"]
  R4 = 220 Ω Resistor [package="0805 [SMD]"]
  R5 = 220 Ω Resistor [package="0805 [SMD]"]

nets:
  N1: A1.Pin_9, JP1_Positivo_5v.1
  N2: A1.Pin_11, A1.Pin_65, JP2_Neutro_(GRN).1
  N3: A1.Pin_42, S1.Pin_3, S1.Pin_4, R3.Pin_1
  N4: A1.Pin_49, A1.Pin_50, DS1.DQ, R5.Pin_0
  N5: A1.Pin_51, A1.Pin_52, A1.Pin_64, LED1.anode
  N6: A1.Pin_58, LED2.anode
  N7: DS2.GND, JP2_Neutro_(GRN).3
  N8: DS2.DQ, R4.Pin_0
  N9: DS2.VDD, R4.Pin_1
  N10: DS1.GND, JP2_Neutro_(GRN).2
  N11: DS1.VDD, JP1_Positivo_5v.3, R5.Pin_1
  N12: LED1.cathode, JP2_Neutro_(GRN).4
  N13: LED2.cathode, JP2_Neutro_(GRN).5
  N14: JP1_Positivo_5v.4, R3.Pin_0
  N15: JP2_Neutro_(GRN).6, S1.Pin_1

custom parts:
  WeMos D1 R1: The WeMos D1 is a ESP8266 WiFi based board that uses the Arduino layout with a operating voltage of 3.3V.
  Resistor: Resistor Basic schematic elements and footprints for 0603, 1206, and PTH resistors.
  220 Ω Resistor: A generic resistor
