# Fritzing sketch 3sensoresWifi05 (saved by Fritzing 1.0.1rc)

parts:
  A1 = WeMos D1 R1
  DS1 = DS18B20 1-Wire Temperature Sensor Probe
  LED1 = smd LED [color="Red (633nm)" package="0805 [SMD]"]
  LED2 = smd LED [color="Green (565nm)" package="0805 [SMD]"]
  JP1_Positivo_5v = Header 12 [package=1x12_machine-pin-header_lock.004]
  JP2_Neutro_(GRN) = Header 12 [package=1x12_machine-pin-header_lock.004]
  S1 = Pushbutton [package="[THT]"]
  R3 = Resistor [package="2010 [SMD]"]
  R5 = 220 Ω Resistor [package="0805 [SMD]"]
  R6 = Resistor [package="2010 [SMD]"]
  S2 = SWITCH-MOMENTARY-2 [package=tactile-switch-1101ne]
  R7 = Resistor [package="2010 [SMD]"]  # not connected
  S3 = SWITCH-MOMENTARY-2 [package=tactile-switch-1101ne]

nets:
  N1: A1.Pin_9, JP1_Positivo_5v.1
  N2: A1.Pin_11, A1.Pin_65, JP2_Neutro_(GRN).1
  N3: A1.Pin_46, A1.Pin_69, DS1.DQ, R5.Pin_0
  N4: A1.Pin_50, S3.1
  N5: A1.Pin_52, A1.Pin_64, LED2.anode, R6.Pin_0
  N6: A1.Pin_53, A1.Pin_62, LED1.anode
  N7: A1.Pin_55, A1.Pin_60, S1.Pin_3, S1.Pin_4, R3.Pin_1
  N8: DS1.GND, JP2_Neutro_(GRN).2
  N9: DS1.VDD, JP1_Positivo_5v.3, R5.Pin_1
  N10: LED1.cathode, JP2_Neutro_(GRN).4
  N11: LED2.cathode, JP2_Neutro_(GRN).5
  N12: JP1_Positivo_5v.4, R3.Pin_0
  N13: JP1_Positivo_5v.11, S3.2
  N14: JP1_Positivo_5v.12, S2.2
  N15: JP2_Neutro_(GRN).6, S1.Pin_1
  N16: JP2_Neutro_(GRN).7, R6.Pin_1

notes:
  Sensor de puerta
  Sensor de Compresor
  wemos d1 pin 13 D11/mosi/d7
  wemos d1 pin 12 d12/miso/d6
  wemos d1 pin 2 tx1/09
  wemos d1 pin 4
  d14/sda/d4

custom parts:
  WeMos D1 R1: The WeMos D1 is a ESP8266 WiFi based board that uses the Arduino layout with a operating voltage of 3.3V.
  Resistor: Resistor Basic schematic elements and footprints for 0603, 1206, and PTH resistors.
  220 Ω Resistor: A generic resistor
